// Logisim project FEIBO.circ as structural Verilog: 7 circuits, main circuit main
module main (
  input  [31:0] N,
  output [31:0] NOUT
);

  wire clock_1_out, comparator_1_eq, comparator_2_eq, comparator_2_gt, multiplexer_1_out, multiplexer_2_out,
       or_1_out;
  wire [4:0] counter_1_q;
  wire [5:5] counter_1_q_2;
  wire [31:0] cmp_1_out_10, cmp_1_out_11, cmp_1_out_12, cmp_1_out_13, cmp_1_out_14, cmp_1_out_15,
       cmp_1_out_16, cmp_1_out_17, multiplexer_4_out, multiplexer_5_out, multiplexer_6_out,
       multiplexer_7_out, multiplexer_8_out, multiplexer_9_out, multiplexer_10_out, multiplexer_11_out,
       register_1_q, register_2_q, register_3_q, register_4_q, register_5_q, register_6_q, register_7_q,
       register_8_q;

  Multiplexer #(.select(5)) multiplexer_1 (
    .in0(N[0]), .in1(N[1]), .in2(N[2]), .in3(N[3]), .in4(N[4]), .in5(N[5]), .in6(N[6]), .in7(N[7]),
    .in8(N[8]), .in9(N[9]), .in10(N[10]), .in11(N[11]), .in12(N[12]), .in13(N[13]), .in14(N[14]),
    .in15(N[15]), .in16(N[16]), .in17(N[17]), .in18(N[18]), .in19(N[19]), .in20(N[20]), .in21(N[21]),
    .in22(N[22]), .in23(N[23]), .in24(N[24]), .in25(N[25]), .in26(N[26]), .in27(N[27]), .in28(N[28]),
    .in29(N[29]), .in30(N[30]), .in31(N[31]), .out(multiplexer_1_out), .sel(counter_1_q));  // open: en
  Multiplexer multiplexer_2 (
    .in0(multiplexer_1_out), .in1(1'b0), .out(multiplexer_2_out), .sel(counter_1_q_2[5]));  // open: en
  cmp cmp_1 (
    .b11(multiplexer_7_out), .b12(multiplexer_8_out), .b21(multiplexer_9_out), .b22(multiplexer_10_out),
    .a11(multiplexer_11_out), .a12(multiplexer_4_out), .a21(multiplexer_5_out), .a22(multiplexer_6_out),
    .in_9(multiplexer_2_out), .out_10(cmp_1_out_10), .out_11(cmp_1_out_11), .out_12(cmp_1_out_12),
    .out_13(cmp_1_out_13), .out_14(cmp_1_out_14), .out_15(cmp_1_out_15), .out_16(cmp_1_out_16),
    .out_17(cmp_1_out_17));
  Comparator #(.width(6), .mode("unsigned")) comparator_1 (
    .a({counter_1_q_2[5], counter_1_q}), .b({6{1'b0}}), .eq(comparator_1_eq));  // open: gt, lt
  Comparator #(.width(6), .mode("unsigned")) comparator_2 (
    .a({counter_1_q_2[5], counter_1_q}), .b(6'b100000), .gt(comparator_2_gt), .eq(comparator_2_eq));  // open: lt
  Counter #(.width(6), .max('h3f)) counter_1 (
    .Q({counter_1_q_2[5], counter_1_q}), .clk(clock_1_out));  // open: load, D, count, carry, clr
  Clock clock_1 (.out(clock_1_out));
  or or_1 (or_1_out, comparator_2_gt, comparator_2_eq);
  Register #(.width(32)) register_1 (.D(cmp_1_out_10), .Q(register_1_q), .clk(clock_1_out));  // open: en, clr
  Register #(.width(32)) register_2 (.D(cmp_1_out_14), .Q(register_2_q), .clk(clock_1_out));  // open: en, clr
  Register #(.width(32)) register_3 (.D(cmp_1_out_15), .Q(register_3_q), .clk(clock_1_out));  // open: en, clr
  Register #(.width(32)) register_4 (.D(cmp_1_out_16), .Q(register_4_q), .clk(clock_1_out));  // open: en, clr
  Register #(.width(32)) register_5 (.D(cmp_1_out_17), .Q(register_5_q), .clk(clock_1_out));  // open: en, clr
  Multiplexer #(.width(32)) multiplexer_3 (
    .in0({32{1'b0}}), .in1(register_3_q), .out(NOUT), .sel(or_1_out));  // open: en
  Register #(.width(32)) register_6 (.D(cmp_1_out_11), .Q(register_6_q), .clk(clock_1_out));  // open: en, clr
  Register #(.width(32)) register_7 (.D(cmp_1_out_12), .Q(register_7_q), .clk(clock_1_out));  // open: en, clr
  Register #(.width(32)) register_8 (.D(cmp_1_out_13), .Q(register_8_q), .clk(clock_1_out));  // open: en, clr
  Multiplexer #(.width(32)) multiplexer_4 (
    .in0(register_3_q), .in1({32{1'b0}}), .out(multiplexer_4_out), .sel(comparator_1_eq));  // open: en
  Multiplexer #(.width(32)) multiplexer_5 (
    .in0(register_4_q), .in1({32{1'b0}}), .out(multiplexer_5_out), .sel(comparator_1_eq));  // open: en
  Multiplexer #(.width(32)) multiplexer_6 (
    .in0(register_5_q), .in1(32'h1), .out(multiplexer_6_out), .sel(comparator_1_eq));  // open: en
  Multiplexer #(.width(32)) multiplexer_7 (
    .in0(register_1_q), .in1(32'h1), .out(multiplexer_7_out), .sel(comparator_1_eq));  // open: en
  Multiplexer #(.width(32)) multiplexer_8 (
    .in0(register_6_q), .in1(32'h1), .out(multiplexer_8_out), .sel(comparator_1_eq));  // open: en
  Multiplexer #(.width(32)) multiplexer_9 (
    .in0(register_7_q), .in1(32'h1), .out(multiplexer_9_out), .sel(comparator_1_eq));  // open: en
  Multiplexer #(.width(32)) multiplexer_10 (
    .in0(register_8_q), .in1({32{1'b0}}), .out(multiplexer_10_out), .sel(comparator_1_eq));  // open: en
  Multiplexer #(.width(32)) multiplexer_11 (
    .in0(register_2_q), .in1(32'h1), .out(multiplexer_11_out), .sel(comparator_1_eq));  // open: en
endmodule

module _32_Adder_32bit (
  input  [31:0] in_1,
  input  [31:0] in_2,
  input  [31:0] _2,
  input  [31:0] in_4,
  input  [31:0] in_5,
  input  [31:0] in_6,
  input  [31:0] in_7,
  input  [31:0] in_8,
  input  [31:0] in_9,
  input  [31:0] in_10,
  input  [31:0] in_11,
  input  [31:0] in_12,
  input  [31:0] in_13,
  input  [31:0] in_14,
  input  [31:0] in_15,
  input  [31:0] in_16,
  input  [31:0] in_17,
  input  [31:0] in_18,
  input  [31:0] in_19,
  input  [31:0] in_20,
  input  [31:0] in_21,
  input  [31:0] in_22,
  input  [31:0] in_23,
  input  [31:0] in_24,
  input  [31:0] in_25,
  input  [31:0] in_26,
  input  [31:0] in_27,
  input  [31:0] in_28,
  input  [31:0] in_29,
  input  [31:0] in_30,
  input  [31:0] in_31,
  input  [31:0] in_32,
  output [31:0] out_33
);

  wire adder_1_cout, adder_2_cout, adder_3_cout, adder_4_cout, adder_5_cout, adder_6_cout, adder_7_cout,
       adder_8_cout, adder_9_cout, adder_10_cout, adder_11_cout, adder_12_cout, adder_14_cout, adder_15_cout,
       adder_16_cout, adder_17_cout, adder_18_cout, adder_19_cout, adder_20_cout, adder_21_cout,
       adder_22_cout, adder_23_cout, adder_24_cout, adder_25_cout, adder_26_cout, adder_29_cout;
  wire [31:0] adder_1_out, adder_2_out, adder_3_out, adder_4_out, adder_5_out, adder_6_out, adder_7_out,
       adder_8_out, adder_9_out, adder_10_out, adder_11_out, adder_12_out, adder_13_out, adder_14_out,
       adder_15_out, adder_16_out, adder_17_out, adder_18_out, adder_19_out, adder_20_out, adder_21_out,
       adder_22_out, adder_23_out, adder_24_out, adder_25_out, adder_26_out, adder_27_out, adder_28_out,
       adder_29_out, adder_30_out;

  Adder #(.width(32)) adder_1 (.a(in_7), .b(in_8), .out(adder_1_out), .cin(adder_16_cout), .cout(adder_1_cout));
  Adder #(.width(32)) adder_2 (.a(in_9), .b(in_10), .out(adder_2_out), .cin(adder_1_cout), .cout(adder_2_cout));
  Adder #(.width(32)) adder_3 (.a(in_11), .b(in_12), .out(adder_3_out), .cin(adder_2_cout), .cout(adder_3_cout));
  Adder #(.width(32)) adder_4 (.a(in_13), .b(in_14), .out(adder_4_out), .cin(adder_3_cout), .cout(adder_4_cout));
  Adder #(.width(32)) adder_5 (.a(in_15), .b(in_16), .out(adder_5_out), .cin(adder_4_cout), .cout(adder_5_cout));
  Adder #(.width(32)) adder_6 (.a(in_17), .b(in_18), .out(adder_6_out), .cin(adder_5_cout), .cout(adder_6_cout));
  Adder #(.width(32)) adder_7 (.a(in_19), .b(in_20), .out(adder_7_out), .cin(adder_6_cout), .cout(adder_7_cout));
  Adder #(.width(32)) adder_8 (.a(in_21), .b(in_22), .out(adder_8_out), .cin(adder_7_cout), .cout(adder_8_cout));
  Adder #(.width(32)) adder_9 (.a(in_23), .b(in_24), .out(adder_9_out), .cin(adder_8_cout), .cout(adder_9_cout));
  Adder #(.width(32)) adder_10 (.a(in_25), .b(in_26), .out(adder_10_out), .cin(adder_9_cout), .cout(adder_10_cout));
  Adder #(.width(32)) adder_11 (.a(in_27), .b(in_28), .out(adder_11_out), .cin(adder_10_cout), .cout(adder_11_cout));
  Adder #(.width(32)) adder_12 (.a(in_29), .b(in_30), .out(adder_12_out), .cin(adder_11_cout), .cout(adder_12_cout));
  Adder #(.width(32)) adder_13 (.a(in_31), .b(in_32), .out(adder_13_out), .cin(adder_12_cout));  // open: cout
  Adder #(.width(32)) adder_14 (.a(in_1), .b(in_2), .out(adder_14_out), .cout(adder_14_cout));  // open: cin
  Adder #(.width(32)) adder_15 (.a(_2), .b(in_4), .out(adder_15_out), .cin(adder_14_cout), .cout(adder_15_cout));
  Adder #(.width(32)) adder_16 (.a(in_5), .b(in_6), .out(adder_16_out), .cin(adder_15_cout), .cout(adder_16_cout));
  Adder #(.width(32)) adder_17 (
    .a(adder_14_out), .b(adder_15_out), .out(adder_17_out), .cout(adder_17_cout));  // open: cin
  Adder #(.width(32)) adder_18 (
    .a(adder_17_out), .b(adder_19_out), .out(adder_18_out), .cout(adder_18_cout));  // open: cin
  Adder #(.width(32)) adder_19 (
    .a(adder_16_out), .b(adder_1_out), .out(adder_19_out), .cin(adder_17_cout), .cout(adder_19_cout));
  Adder #(.width(32)) adder_20 (
    .a(adder_2_out), .b(adder_3_out), .out(adder_20_out), .cin(adder_19_cout), .cout(adder_20_cout));
  Adder #(.width(32)) adder_21 (
    .a(adder_20_out), .b(adder_22_out), .out(adder_21_out), .cin(adder_18_cout), .cout(adder_21_cout));
  Adder #(.width(32)) adder_22 (
    .a(adder_4_out), .b(adder_5_out), .out(adder_22_out), .cin(adder_20_cout), .cout(adder_22_cout));
  Adder #(.width(32)) adder_23 (
    .a(adder_6_out), .b(adder_7_out), .out(adder_23_out), .cin(adder_22_cout), .cout(adder_23_cout));
  Adder #(.width(32)) adder_24 (
    .a(adder_23_out), .b(adder_25_out), .out(adder_24_out), .cin(adder_21_cout), .cout(adder_24_cout));
  Adder #(.width(32)) adder_25 (
    .a(adder_8_out), .b(adder_9_out), .out(adder_25_out), .cin(adder_23_cout), .cout(adder_25_cout));
  Adder #(.width(32)) adder_26 (
    .a(adder_10_out), .b(adder_11_out), .out(adder_26_out), .cin(adder_25_cout), .cout(adder_26_cout));
  Adder #(.width(32)) adder_27 (
    .a(adder_26_out), .b(adder_28_out), .out(adder_27_out), .cin(adder_24_cout));  // open: cout
  Adder #(.width(32)) adder_28 (
    .a(adder_12_out), .b(adder_13_out), .out(adder_28_out), .cin(adder_26_cout));  // open: cout
  Adder #(.width(32)) adder_29 (
    .a(adder_18_out), .b(adder_21_out), .out(adder_29_out), .cout(adder_29_cout));  // open: cin
  Adder #(.width(32)) adder_30 (
    .a(adder_24_out), .b(adder_27_out), .out(adder_30_out), .cin(adder_29_cout));  // open: cout
  Adder #(.width(32)) adder_31 (.a(adder_29_out), .b(adder_30_out), .out(out_33));  // open: cin, cout

  // Notes on the sheet:
  //   1
  //   4
  //   5
  //   6
  //   7
  //   8
  //   9
  //   10
  //   11
  //   12
  //   13
  //   14
  //   15
  //   16
  //   3
  //   2-1
  //   2-2
  //   2-3
  //   2-4
  //   2-5
  //   2-6
  //   2-7
  //   2-8
  //   3-1
  //   3-2
  //   3-3
  //   3-4
  //   4-2
endmodule

module compute (
  input  [31:0] _1,
  input  [31:0] _2,
  input  [31:0] _3,
  input  [31:0] _4,
  output [31:0] out_5
);

  wire [31:0] multiplier_1_out, multiplier_2_out;

  Multiplier #(.width(32)) multiplier_1 (.a(_1), .b(_3), .out(multiplier_1_out));  // open: cin, cout
  Multiplier #(.width(32)) multiplier_2 (.a(_2), .b(_4), .out(multiplier_2_out));  // open: cin, cout
  Adder #(.width(32)) adder_1 (.a(multiplier_1_out), .b(multiplier_2_out), .out(out_5));  // open: cin, cout
endmodule

module quick (
  input  [31:0] a11,
  input  [31:0] a12,
  input  [31:0] a21,
  input  [31:0] a22,
  input  [31:0] b11,
  input  [31:0] b12,
  input  [31:0] b21,
  input  [31:0] b22,
  output [31:0] c11,
  output [31:0] c12,
  output [31:0] c2,
  output [31:0] c22
);

  compute compute_1 (._1(a11), ._2(a12), ._3(b11), ._4(b21), .out_5(c11));
  compute compute_2 (._1(a11), ._2(a12), ._3(b12), ._4(b22), .out_5(c12));
  compute compute_3 (._1(a21), ._2(a22), ._3(b12), ._4(b22), .out_5(c22));
  compute compute_4 (._1(a21), ._2(a22), ._3(b11), ._4(b21), .out_5(c2));
endmodule

module select (
  input  [31:0] in,
  input  en,
  input  comp,
  output [31:0] out_4
);

  wire and_1_out;

  and and_1 (and_1_out, en, comp);
  Multiplexer #(.width(32)) multiplexer_1 (.in0(in), .in1({32{1'b0}}), .out(out_4), .sel(and_1_out));  // open: en
endmodule

module cmp (
  input  [31:0] b11,
  input  [31:0] b12,
  input  [31:0] b21,
  input  [31:0] b22,
  input  [31:0] a11,
  input  [31:0] a12,
  input  [31:0] a21,
  input  [31:0] a22,
  input  in_9,
  output [31:0] out_10,
  output [31:0] out_11,
  output [31:0] out_12,
  output [31:0] out_13,
  output [31:0] out_14,
  output [31:0] out_15,
  output [31:0] out_16,
  output [31:0] out_17
);

  wire comparator_1_eq;
  wire [31:0] quick_1_c2, quick_1_c11, quick_1_c12, quick_1_c22;

  mul mul_1 (
    .in_1(b11), .in_2(b12), .in_3(b21), .in_4(b22), .out_5(out_10), .out_6(out_11), .out_7(out_12),
    .out_8(out_13));
  quick quick_1 (
    .a11(b11), .a12(b12), .a21(b21), .a22(b22), .b11(a11), .b12(a12), .b21(a21), .b22(a22),
    .c11(quick_1_c11), .c12(quick_1_c12), .c2(quick_1_c2), .c22(quick_1_c22));
  Comparator #(.width(1)) comparator_1 (.a(in_9), .b(1'b0), .eq(comparator_1_eq));  // open: gt, lt
  Multiplexer #(.width(32)) multiplexer_1 (
    .in0(quick_1_c11), .in1(a11), .out(out_14), .sel(comparator_1_eq));  // open: en
  Multiplexer #(.width(32)) multiplexer_2 (
    .in0(quick_1_c12), .in1(a12), .out(out_15), .sel(comparator_1_eq));  // open: en
  Multiplexer #(.width(32)) multiplexer_3 (
    .in0(quick_1_c2), .in1(a21), .out(out_16), .sel(comparator_1_eq));  // open: en
  Multiplexer #(.width(32)) multiplexer_4 (
    .in0(quick_1_c22), .in1(a22), .out(out_17), .sel(comparator_1_eq));  // open: en
endmodule

module mul (
  input  [31:0] in_1,
  input  [31:0] in_2,
  input  [31:0] in_3,
  input  [31:0] in_4,
  output [31:0] out_5,
  output [31:0] out_6,
  output [31:0] out_7,
  output [31:0] out_8
);

  compute compute_1 (._1(in_3), ._2(in_4), ._3(in_1), ._4(in_3), .out_5(out_7));
  compute compute_2 (._1(in_3), ._2(in_4), ._3(in_2), ._4(in_4), .out_5(out_8));
  compute compute_3 (._1(in_1), ._2(in_2), ._3(in_1), ._4(in_3), .out_5(out_5));
  compute compute_4 (._1(in_1), ._2(in_2), ._3(in_2), ._4(in_4), .out_5(out_6));

  // Notes on the sheet:
  //   11
  //   12
  //   22
  //   21
  //   11
  //   12
  //   21
  //   22
endmodule
