// Logisim project MOD.circ as structural Verilog
module mod5 (
  input  in,
  output S0,
  output S1,
  output S2,
  output S3,
  output S4
);

  wire clock_1_out, not_1_out, not_2_out, register_1_q;

  not not_1 (not_1_out, in);
  Register #(.width(1)) register_1 (.D(in), .Q(register_1_q), .clk(clock_1_out));  // open: en, clr
  Clock clock_1 (.out(clock_1_out));
  not not_2 (not_2_out, register_1_q);
  and and_1 (S2, not_2_out, in);
  and and_2 (S3, register_1_q, in);
  and and_3 (S4, register_1_q, not_1_out);
  and and_4 (S1, not_1_out, not_2_out);

  assign S0 = 1'b0;
endmodule
