// Logisim project SR.circ as structural Verilog: 1 circuit, main circuit main
module main (
  input  R,
  input  S,
  output Q,
  output nQ
);

  wire or_1_out, or_2_out;

  or or_1 (or_1_out, R, nQ);
  or or_2 (or_2_out, Q, S);
  not not_1 (Q, or_1_out);
  not not_2 (nQ, or_2_out);

  // Notes on the sheet:
  //   SR锁存器
endmodule
