// Logisim project feibonaqie.circ as structural Verilog: 1 circuit, main circuit main
module main (
  input  [2:0] N,
  output [3:0] Nth
);

  wire clock_1_out, comparator_1_lt, comparator_2_eq, comparator_2_lt, not_1_out, or_1_out;
  wire [3:0] adder_1_out, multiplexer_1_out, multiplexer_2_out, multiplexer_3_out, r1_q, r2_q;
  wire [5:0] counter_q;

  Counter #(.width(6), .max('h3f)) counter (.Q(counter_q), .clk(clock_1_out));  // open: load, D, count, carry, clr
  Comparator #(.width(6), .mode("unsigned")) comparator_1 (
    .a(counter_q), .b(6'b000010), .lt(comparator_1_lt));  // open: gt, eq
  Register #(.width(4)) r1 (.D(multiplexer_1_out), .Q(r1_q), .clk(clock_1_out));  // open: en, clr
  Multiplexer #(.width(4)) multiplexer_1 (
    .in0(adder_1_out), .in1(4'b0001), .out(multiplexer_1_out), .sel(comparator_1_lt));  // open: en
  Multiplexer #(.width(4)) multiplexer_2 (
    .in0(r1_q), .in1(4'b0000), .out(multiplexer_2_out), .sel(comparator_1_lt));  // open: en
  Clock clock_1 (.out(clock_1_out));
  Comparator #(.width(6), .mode("unsigned")) comparator_2 (
    .a({3'b000, N}), .b(counter_q), .eq(comparator_2_eq), .lt(comparator_2_lt));  // open: gt
  Adder #(.width(4)) adder_1 (.a(r1_q), .b(r2_q), .out(adder_1_out));  // open: cin, cout
  Register #(.width(4)) r2 (.D(multiplexer_2_out), .Q(r2_q), .clk(clock_1_out));  // open: en, clr
  Multiplexer #(.width(4)) multiplexer_3 (
    .in0(4'b0000), .in1(adder_1_out), .out(multiplexer_3_out), .sel(comparator_2_eq));  // open: en
  Register #(.width(4)) register_1 (.D(multiplexer_3_out), .en(not_1_out), .Q(Nth), .clk(clock_1_out));  // open: clr
  not not_1 (not_1_out, or_1_out);
  or or_1 (or_1_out, comparator_2_lt, clock_1_out);
endmodule
