// Logisim project logisim初步.circ as structural Verilog: 1 circuit, main circuit main
module main (
  input  [4:0] in_1,
  output [4:0] _1,
  output [4:0] _2
);


  assign _1 = in_1;
  assign _2 = in_1;
endmodule
