// Logisim project swap.circ as structural Verilog
module _1bit_swap (
  input  I1,
  input  I2,
  input  S,
  output O1,
  output O2
);

  wire and_1_out, and_2_out, and_3_out, and_4_out, not_1_out;

  and and_1 (and_1_out, I1, not_1_out);
  and and_2 (and_2_out, I1, S);
  not not_1 (not_1_out, S);
  and and_3 (and_3_out, I2, I2, S);
  and and_4 (and_4_out, I2, not_1_out);
  or or_1 (O1, and_1_out, and_3_out);
  or or_2 (O2, and_2_out, and_4_out);

  // Notes on the sheet:
  //   1位二进制swap，当S为1时交换
endmodule

// swap
module _4bit_swap (
  input  S1,
  input  [3:0] A,
  input  [3:0] B,
  output [3:0] _1,
  output [3:0] _2
);

  _1bit_swap u_1bit_swap_1 (.I1(A[0]), .I2(B[0]), .S(S1), .O1(_1[0]), .O2(_2[0]));
  _1bit_swap u_1bit_swap_2 (.I1(A[1]), .I2(B[1]), .S(S1), .O1(_1[1]), .O2(_2[1]));
  _1bit_swap u_1bit_swap_3 (.I1(A[2]), .I2(B[2]), .S(S1), .O1(_1[2]), .O2(_2[2]));
  _1bit_swap u_1bit_swap_4 (.I1(A[3]), .I2(B[3]), .S(S1), .O1(_1[3]), .O2(_2[3]));

  // Notes on the sheet:
  //   4位二进制swap，当S为1时交换
endmodule

// cmp
module _1bit_comp (
  input  A,
  input  B,
  output Y3,
  output Y2,
  output Y1
);

  wire not_1_out, not_2_out;

  not not_1 (not_1_out, A);
  not not_2 (not_2_out, B);
  and and_1 (Y3, not_1_out, B);
  and and_2 (Y1, A, not_2_out);
  nor nor_1 (Y2, Y3, Y1);

  // Notes on the sheet:
  //   1位比较器，B>A则交换，输出Y3=1
endmodule

module _4bit_sort (
  input  [3:0] A,
  input  [3:0] B,
  input  [3:0] C,
  input  [3:0] D,
  output [3:0] _1,
  output [3:0] _2,
  output [3:0] _3,
  output [3:0] _4
);

  wire cmp1_y, cmp2_y, cmp3_y, cmp4_y, cmp5_y, not_1_out, not_2_out, not_3_out, not_4_out, not_5_out;
  wire [3:0] swap1__1, swap1__2, swap2__1, swap2__2, swap3__2, swap4__1;

  not not_1 (not_1_out, cmp1_y);
  _4bit_comp cmp1 (.A(A), .B(B), .Y(cmp1_y));
  _4bit_comp cmp2 (.A(C), .B(D), .Y(cmp2_y));
  not not_2 (not_2_out, cmp2_y);
  _4bit_swap swap1 (.S1(not_1_out), .A(A), .B(B), ._1(swap1__1), ._2(swap1__2));
  _4bit_swap swap2 (.S1(not_2_out), .A(C), .B(D), ._1(swap2__1), ._2(swap2__2));
  _4bit_comp cmp3 (.A(swap1__1), .B(swap2__1), .Y(cmp3_y));
  _4bit_comp cmp4 (.A(swap1__2), .B(swap2__2), .Y(cmp4_y));
  not not_3 (not_3_out, cmp3_y);
  not not_4 (not_4_out, cmp4_y);
  _4bit_swap swap3 (.S1(not_3_out), .A(swap1__1), .B(swap2__1), ._1(_1), ._2(swap3__2));
  _4bit_comp cmp5 (.A(swap3__2), .B(swap4__1), .Y(cmp5_y));
  _4bit_swap swap4 (.S1(not_4_out), .A(swap1__2), .B(swap2__2), ._1(swap4__1), ._2(_4));
  _4bit_swap swap5 (.S1(not_5_out), .A(swap3__2), .B(swap4__1), ._1(_2), ._2(_3));
  not not_5 (not_5_out, cmp5_y);

  // Notes on the sheet:
  //   cmp输出B>A，Y值为1，不交换
  //   4个4位二进制排序电路
  //   输出B>A，Y值为1，不交换
endmodule

// cmp
module _4bit_comp (
  input  [3:0] A,
  input  [3:0] B,
  output Y
);

  wire and_1_out, and_2_out, and_3_out, cmp1_y1, cmp1_y2, cmp1_y3, cmp2_y1, cmp2_y2, cmp2_y3, cmp3_y1,
       cmp3_y2, cmp3_y3, cmp4_y1, cmp4_y2, cmp4_y3, not_1_out, not_2_out, not_3_out, not_4_out, not_5_out;

  _1bit_comp cmp1 (.A(A[3]), .B(B[3]), .Y3(cmp1_y3), .Y2(cmp1_y2), .Y1(cmp1_y1));
  not not_1 (not_1_out, cmp1_y1);
  _1bit_comp cmp2 (.A(A[2]), .B(B[2]), .Y3(cmp2_y3), .Y2(cmp2_y2), .Y1(cmp2_y1));
  not not_2 (not_2_out, cmp2_y1);
  and and_1 (and_1_out, cmp1_y2, cmp2_y3, not_1_out);
  _1bit_comp cmp3 (.A(A[1]), .B(B[1]), .Y3(cmp3_y3), .Y2(cmp3_y2), .Y1(cmp3_y1));
  and and_2 (and_2_out, not_2_out, cmp2_y2, not_1_out, cmp3_y3);
  not not_3 (not_3_out, cmp3_y1);
  _1bit_comp cmp4 (.A(A[0]), .B(B[0]), .Y3(cmp4_y3), .Y2(cmp4_y2), .Y1(cmp4_y1));
  not not_4 (not_4_out, cmp4_y2);
  not not_5 (not_5_out, cmp4_y1);
  and and_3 (and_3_out, not_1_out, not_2_out, cmp3_y2, cmp4_y3, not_4_out, not_3_out, not_5_out);
  or or_1 (Y, cmp1_y3, and_1_out, and_2_out, and_3_out);

  // Notes on the sheet:
  //   4位比较器，B>A则输出Y=1
endmodule
