// Logisim project CPU-singel-1.circ as structural Verilog: 8 circuits, main circuit main
module main (
  input  reset,
  output [31:0] out_2,
  output out_3,
  output [4:0] out_4,
  output [31:0] out_5,
  output out_6,
  output [4:0] out_7,
  output [31:0] out_8
);

  wire Alusel, and_1_out, Branch, clk, EXTOp, J, Jal, Jr, MR, MtoR, or_1_out, RegDst, Zero;
  wire [3:0] ALUOp;
  wire [4:0] multiplexer_1_out;
  wire [31:0] dm_1_out_8, ext, multiplexer_3_out, multiplexer_4_out, PC_prime, RD1, result;

  // Probe on out_2[25:0]
  or or_1 (or_1_out, J, Jal);
  and and_1 (and_1_out, Zero, Branch);
  IFU ifu_1 (
    .CLOCK(clk), .reset(reset), .Instr(out_2), .Zero(and_1_out), .beq(ext), .jump(or_1_out), .jr(Jr),
    .index(out_2[25:0]), .pc_4(PC_prime), .ra(RD1));
  // Probe on out_2
  // Probe on out_2[25:21]
  // Probe on out_2[20:16]
  // Probe on out_2[15:11]
  // Probe on out_2[15:0]
  Clock u_CLK (.out(clk));
  // Probe on out_2[5:0]
  // Probe on out_2[31:26]
  Multiplexer #(.width(5), .enable("false")) multiplexer_1 (
    .in0(out_2[20:16]), .in1(out_2[15:11]), .out(multiplexer_1_out), .sel(RegDst));
  Multiplexer #(.width(5), .enable("false")) multiplexer_2 (
    .in0(multiplexer_1_out), .in1({5{1'b1}}), .out(out_4), .sel(Jal));
  Controller controller_1 (
    .OP(out_2[31:26]), .FUNC(out_2[5:0]), .out_3(RegDst), .out_4(Branch), .out_5(MtoR), .out_6(out_6),
    .out_7(MR), .ALUOp(ALUOp), .out_8(Alusel), .out_9(EXTOp), .out_10(out_3), .Jr(Jr), .Jal(Jal), .J(J));
  GRF grf_1 (
    .A1(out_2[25:21]), .A2(out_2[20:16]), .A3(out_4), .WD(out_5), .RD1(RD1), .RD2(out_8), .reset(reset),
    .WE(out_3), .clk(clk));
  // Probe on out_8
  // Probe on RegDst
  // Probe on Branch
  // Probe on MtoR
  // Probe on out_6
  // Probe on MR
  // Probe on ALUOp
  // Probe on Alusel
  // Probe on EXTOp
  // Probe on out_3
  // Probe on RD1
  Multiplexer #(.width(32), .enable("false")) multiplexer_3 (
    .in0(out_8), .in1(ext), .out(multiplexer_3_out), .sel(Alusel));
  ALU alu_1 (.A(RD1), .B(multiplexer_3_out), .OP(ALUOp), .zero(Zero), .OUT({result[31:7], out_7, result[1:0]}));
  // Probe on multiplexer_3_out
  EXT ext_1 (.in_1(out_2[15:0]), .ext_type(EXTOp), .out_3(ext));
  // Probe on ext
  // Probe on {result[31:7], out_7, result[1:0]}
  DM dm_1 (
    .in_1(out_7), .in_2(out_8), .in_3(out_6), .in_5(clk), .in_6(MR), .in_7(reset), .out_8(dm_1_out_8));  // open: in_4
  Multiplexer #(.width(32), .enable("false")) multiplexer_4 (
    .in0(dm_1_out_8), .in1({result[31:7], out_7, result[1:0]}), .out(multiplexer_4_out), .sel(MtoR));
  Multiplexer #(.width(32), .enable("false")) multiplexer_5 (
    .in0(multiplexer_4_out), .in1(PC_prime), .out(out_5), .sel(Jal));
  // Probe on out_5

  // Other names for the same wires on the sheet: Func[5:0] = out_2[5:0]; imm[15:0] = out_2[15:0];
  //   index[25:0] = out_2[25:0]; Instr[31:0] = out_2; Rd[4:0] = out_2[15:11]; Rt[4:0] = out_2[20:16];
  //   Rs[4:0] = out_2[25:21]; Op[5:0] = out_2[31:26]; MW = out_6; RD2[31:0] = out_8; RegA[4:0] = out_4;
  //   MemA[4:0] = out_7; result[6:2] = out_7; RW = out_3; WD[31:0] = out_5
endmodule

module ALU (
  input  [31:0] A,
  input  [31:0] B,
  input  [3:0] OP,
  output zero,
  output [31:0] OUT
);

  wire [1:0] multiplexer_1_out;
  wire [31:0] \与 , \减 , \加 , \或 ;

  Adder #(.width(32)) adder_1 (.a(A), .b(B), .out(\加 ));  // open: cin, cout
  Subtractor #(.width(32)) subtractor_1 (.a(A), .b(B), .out(\减 ));  // open: bin, bout
  assign \与  = A & B;  // AND_Gate 与运算, 32 bits wide
  assign \或  = A | {{16{1'b0}}, B[15:0]};  // OR_Gate 或运算, 32 bits wide
  Multiplexer #(.width(2)) multiplexer_1 (.in0(2'b00), .out(multiplexer_1_out), .sel(1'b0), .en(OP[0]));  // open: in1
  Multiplexer #(.width(2)) multiplexer_2 (.in0(2'b01), .out(multiplexer_1_out), .sel(1'b0), .en(OP[1]));  // open: in1
  Multiplexer #(.width(2)) multiplexer_3 (.in0(2'b10), .out(multiplexer_1_out), .sel(1'b0), .en(OP[2]));  // open: in1
  Multiplexer #(.width(2)) multiplexer_4 (.in0(2'b11), .out(multiplexer_1_out), .sel(1'b0), .en(OP[3]));  // open: in1
  // Probe on OUT
  Multiplexer #(.select(2), .width(32), .enable("false")) multiplexer_5 (
    .in0(\加 ), .in1(\减 ), .in2(\或 ), .in3({B[15:0], {16{1'b0}}}), .out(OUT), .sel(multiplexer_1_out));
  Comparator #(.width(32)) comparator_1 (.a({32{1'b0}}), .b(\减 ), .eq(zero));  // open: gt, lt

  // Other names for the same wires on the sheet: LUI[31:16] = B[15:0]

  // Notes on the sheet:
  //   LUI指令
  //   beq置1
endmodule

module GRF (
  input  reset,
  input  WE,
  input  clk,
  input  [4:0] A1,
  input  [4:0] A2,
  input  [4:0] A3,
  input  [31:0] WD,
  output [31:0] RD1,
  output [31:0] RD2
);

  GRF_register grf_register_1 (
    .IN(A1), .A(WD), .IN2(A3), .IN1(A2), .CLK(clk), .RESET(reset), .enable(WE), .out(RD1), .out2(RD2));
endmodule

// register
module GRF_register (
  input  enable,
  input  RESET,
  input  CLK,
  input  [4:0] IN,
  input  [31:0] A,
  input  [4:0] IN2,
  input  [4:0] IN1,
  output [31:0] out,
  output [31:0] out2
);

  wire [31:0] _1, _2, _3, _4, _5, _6, _7, _8, _9, _10, _11, _12, _13, _14, _15, _16, _17, _18, _19, _20, _21,
       _22, _23, _24, _25, _26, _27, _28, _29, _30, _31, _32, D2, D3, D4, D5, D6, D7, D8, D9, D10, D11, D12,
       D13, D14, D15, D16, D17, D18, D19, D20, D21, D22, D23, D24, D25, D26, D27, D28, D29, D30, D31, D32;

  Register #(.width(32)) R1 (.D({32{1'b0}}), .Q(_1), .clk(CLK), .clr(RESET));  // open: en
  Register #(.width(32)) R9 (.D(D9), .Q(_9), .clk(CLK), .clr(RESET));  // open: en
  Register #(.width(32)) R17 (.D(D17), .Q(_17), .clk(CLK), .clr(RESET));  // open: en
  Register #(.width(32)) R25 (.D(D25), .Q(_25), .clk(CLK), .clr(RESET));  // open: en
  Demultiplexer #(.select(5), .width(32), .tristate("true")) demultiplexer_1 (
    .out1(D2), .out2(D3), .out3(D4), .out4(D5), .out5(D6), .out6(D7), .out7(D8), .out8(D9), .out9(D10),
    .out10(D11), .out11(D12), .out12(D13), .out13(D14), .out14(D15), .out15(D16), .out16(D17), .out17(D18),
    .out18(D19), .out19(D20), .out20(D21), .out21(D22), .out22(D23), .out23(D24), .out24(D25), .out25(D26),
    .out26(D27), .out27(D28), .out28(D29), .out29(D30), .out30(D31), .out31(D32), .in(A), .sel(IN2),
    .en(enable));  // open: out0
  Register #(.width(32)) R2 (.D(D2), .Q(_2), .clk(CLK), .clr(RESET));  // open: en
  Register #(.width(32)) R10 (.D(D10), .Q(_10), .clk(CLK), .clr(RESET));  // open: en
  Register #(.width(32)) R18 (.D(D18), .Q(_18), .clk(CLK), .clr(RESET));  // open: en
  Register #(.width(32)) R26 (.D(D26), .Q(_26), .clk(CLK), .clr(RESET));  // open: en
  Register #(.width(32)) R3 (.D(D3), .Q(_3), .clk(CLK), .clr(RESET));  // open: en
  Register #(.width(32)) R11 (.D(D11), .Q(_11), .clk(CLK), .clr(RESET));  // open: en
  Register #(.width(32)) R19 (.D(D19), .Q(_19), .clk(CLK), .clr(RESET));  // open: en
  Register #(.width(32)) R27 (.D(D27), .Q(_27), .clk(CLK), .clr(RESET));  // open: en
  Register #(.width(32)) R4 (.D(D4), .Q(_4), .clk(CLK), .clr(RESET));  // open: en
  Register #(.width(32)) R12 (.D(D12), .Q(_12), .clk(CLK), .clr(RESET));  // open: en
  Register #(.width(32)) R20 (.D(D20), .Q(_20), .clk(CLK), .clr(RESET));  // open: en
  Register #(.width(32)) R28 (.D(D28), .Q(_28), .clk(CLK), .clr(RESET));  // open: en
  Register #(.width(32)) R5 (.D(D5), .Q(_5), .clk(CLK), .clr(RESET));  // open: en
  Register #(.width(32)) R13 (.D(D13), .Q(_13), .clk(CLK), .clr(RESET));  // open: en
  Register #(.width(32)) R21 (.D(D21), .Q(_21), .clk(CLK), .clr(RESET));  // open: en
  Register #(.width(32)) R29 (.D(D29), .Q(_29), .clk(CLK), .clr(RESET));  // open: en
  Register #(.width(32)) R6 (.D(D6), .Q(_6), .clk(CLK), .clr(RESET));  // open: en
  Register #(.width(32)) R14 (.D(D14), .Q(_14), .clk(CLK), .clr(RESET));  // open: en
  Register #(.width(32)) R22 (.D(D22), .Q(_22), .clk(CLK), .clr(RESET));  // open: en
  Register #(.width(32)) R30 (.D(D30), .Q(_30), .clk(CLK), .clr(RESET));  // open: en
  Register #(.width(32)) R7 (.D(D7), .Q(_7), .clk(CLK), .clr(RESET));  // open: en
  Register #(.width(32)) R15 (.D(D15), .Q(_15), .clk(CLK), .clr(RESET));  // open: en
  Register #(.width(32)) R23 (.D(D23), .Q(_23), .clk(CLK), .clr(RESET));  // open: en
  Register #(.width(32)) R31 (.D(D31), .Q(_31), .clk(CLK), .clr(RESET));  // open: en
  Register #(.width(32)) R8 (.D(D8), .Q(_8), .clk(CLK), .clr(RESET));  // open: en
  Register #(.width(32)) R16 (.D(D16), .Q(_16), .clk(CLK), .clr(RESET));  // open: en
  Register #(.width(32)) R24 (.D(D24), .Q(_24), .clk(CLK), .clr(RESET));  // open: en
  Register #(.width(32)) R32 (.D(D32), .Q(_32), .clk(CLK), .clr(RESET));  // open: en
  Multiplexer #(.select(5), .width(32)) multiplexer_1 (
    .in0(_1), .in1(_2), .in2(_3), .in3(_4), .in4(_5), .in5(_6), .in6(_7), .in7(_8), .in8(_9), .in9(_10),
    .in10(_11), .in11(_12), .in12(_13), .in13(_14), .in14(_15), .in15(_16), .in16(_17), .in17(_18),
    .in18(_19), .in19(_20), .in20(_21), .in21(_22), .in22(_23), .in23(_24), .in24(_25), .in25(_26),
    .in26(_27), .in27(_28), .in28(_29), .in29(_30), .in30(_31), .in31(_32), .out(out), .sel(IN));  // open: en
  Multiplexer #(.select(5), .width(32)) multiplexer_2 (
    .in0(_1), .in1(_2), .in2(_3), .in3(_4), .in4(_5), .in5(_6), .in6(_7), .in7(_8), .in8(_9), .in9(_10),
    .in10(_11), .in11(_12), .in12(_13), .in13(_14), .in14(_15), .in15(_16), .in16(_17), .in17(_18),
    .in18(_19), .in19(_20), .in20(_21), .in21(_22), .in22(_23), .in23(_24), .in24(_25), .in25(_26),
    .in26(_27), .in27(_28), .in28(_29), .in29(_30), .in30(_31), .in31(_32), .out(out2), .sel(IN1));  // open: en

  // Other names for the same wires on the sheet: EN = enable
endmodule

module Controller (
  input  [5:0] OP,
  input  [5:0] FUNC,
  output out_3,
  output out_4,
  output out_5,
  output out_6,
  output out_7,
  output out_8,
  output out_9,
  output out_10,
  output [3:0] ALUOp,
  output Jr,
  output Jal,
  output J
);

  wire add, beq, lw, not_1_out, not_2_out, not_3_out, not_4_out, not_5_out, not_6_out, not_7_out, not_8_out,
       not_9_out, not_10_out, not_11_out, not_12_out, sub, sw;

  not not_1 (not_1_out, OP[5]);
  not not_2 (not_2_out, OP[2]);
  not not_3 (not_3_out, OP[3]);
  not not_4 (not_4_out, OP[4]);
  not not_5 (not_5_out, OP[0]);
  not not_6 (not_6_out, OP[1]);
  not not_7 (not_7_out, FUNC[5]);
  not not_8 (not_8_out, FUNC[4]);
  not not_9 (not_9_out, FUNC[2]);
  not not_10 (not_10_out, FUNC[3]);
  not not_11 (not_11_out, FUNC[0]);
  not not_12 (not_12_out, FUNC[1]);
  and u_add (add, not_1_out, not_4_out, not_3_out, not_2_out, not_6_out, not_5_out, FUNC[5], not_8_out, not_10_out, not_9_out, not_12_out, FUNC[0]);
  and ori (ALUOp[2], not_1_out, not_4_out, OP[3], OP[2], not_6_out, OP[0]);
  and lui (ALUOp[3], not_1_out, not_4_out, OP[3], OP[2], OP[1], OP[0]);
  and u_lw (lw, OP[5], not_4_out, not_3_out, not_2_out, OP[1], OP[0]);
  and u_sw (sw, OP[5], not_4_out, OP[3], not_2_out, OP[1], OP[0]);
  and u_beq (beq, not_1_out, not_4_out, not_3_out, OP[2], not_6_out, not_5_out);
  and u_j (J, not_1_out, not_4_out, not_3_out, not_2_out, OP[1], not_5_out);
  and u_jal (Jal, not_1_out, not_4_out, not_3_out, not_2_out, OP[1], OP[0]);
  and u_jr (Jr, not_1_out, not_4_out, not_3_out, not_2_out, not_6_out, not_5_out, not_7_out, not_8_out, FUNC[3], not_9_out, not_12_out, not_11_out);
  and u_sub (sub, not_1_out, not_4_out, not_3_out, not_2_out, not_6_out, not_5_out, FUNC[5], not_8_out, not_10_out, not_9_out, FUNC[1], FUNC[0]);
  or RegDst (out_3, add, sub);
  buf Branch (out_4, beq);  // OR_Gate
  or MtoR (out_5, add, sub, ALUOp[2], ALUOp[3]);
  buf MW (out_6, sw);  // OR_Gate
  buf MR (out_7, lw);  // OR_Gate
  or or_1 (ALUOp[1], beq, sub);
  or or_2 (ALUOp[0], sw, lw, add);
  or ALUsel (out_8, sw, lw, ALUOp[3], ALUOp[2]);
  buf EXTOp (out_9, beq);  // OR_Gate
  or RW (out_10, lw, ALUOp[3], ALUOp[2], sub, add, Jal);

  // Other names for the same wires on the sheet: ori = ALUOp[2]; lui = ALUOp[3]
endmodule

module DM (
  input  [4:0] in_1,
  input  [31:0] in_2,
  input  in_3,
  input  in_4,
  input  in_5,
  input  in_6,
  input  in_7,
  output [31:0] out_8
);

  RAM #(.addrWidth(5), .dataWidth(32), .bus("separate")) ram_1 (
    .addr(in_1), .din(in_2), .data(out_8), .str(in_3), .sel(in_4), .clk(in_5), .ld(in_6), .clr(in_7));
endmodule

module IFU (
  input  [31:0] beq,
  input  Zero,
  input  CLOCK,
  input  [25:0] index,
  input  reset,
  input  [31:0] ra,
  input  jump,
  input  jr,
  output [31:0] pc_4,
  output [31:0] Instr
);

  wire [31:0] adder_1_out, multiplexer_1_out, PC, PC_prime;

  Register #(.width(32)) register_1 (.D(PC_prime), .Q(PC), .clk(CLOCK), .clr(reset));  // open: en
  ROM #(.addrWidth(5), .dataWidth(32)) rom_1 (.addr(PC[6:2]), .data(Instr));  // open: sel
  // Probe on PC
  Adder #(.width(32)) adder_1 (.a(PC), .b(beq), .out(adder_1_out));  // open: cin, cout
  Multiplexer #(.width(32)) multiplexer_1 (
    .in0(PC), .in1(adder_1_out), .out(multiplexer_1_out), .sel(Zero));  // open: en
  Adder #(.width(32)) adder_2 (.a(32'h4), .b(multiplexer_1_out), .out(pc_4));  // open: cin, cout
  Multiplexer #(.select(2), .width(32), .enable("false")) multiplexer_2 (
    .in0(pc_4), .in1({PC[31:28], index, 2'b00}), .in2(ra), .out(PC_prime), .sel({jr, jump}));  // open: in3
  // Probe on PC_prime

  // Other names for the same wires on the sheet: sel[1:0] = {jr, jump}

  // Notes on the sheet:
  //   2-6bit
  //   contents of rom_1 (hex, n*v repeats v):
  //   3404007b 340501c8 3c0600ea 858021 868821 a49023 859823 34080000 ad040000 ad050004 8d040000 8d050004
  //   ad040004 ad050000
  //   PC-Adder
endmodule

module EXT (
  input  [15:0] in_1,
  input  ext_type,
  output [31:0] out_3
);

  wire [31:0] bit_extender_1_out, bit_extender_2_out;

  assign bit_extender_1_out = {{16{in_1[15]}}, in_1};  // Bit_Extender bit_extender_1
  assign bit_extender_2_out = {{14{in_1[15]}}, {in_1, 2'b00}};  // Bit_Extender bit_extender_2
  Multiplexer #(.width(32)) multiplexer_1 (
    .in0(bit_extender_1_out), .in1(bit_extender_2_out), .out(out_3), .sel(ext_type));  // open: en

  // Notes on the sheet:
  //   R型ext
  //   beq跳转地址
endmodule
