// Logisim project 4bits-ALU.circ as structural Verilog
module alu (
  input  [3:0] A,
  input  [3:0] B,
  input  [1:0] OP,
  output [3:0] OUT
);

  wire [3:0] \与 , \减 , \加 , \或 ;

  Adder #(.width(4)) adder_1 (.a(A), .b(B), .out(\加 ));  // open: cin, cout
  Subtractor #(.width(4)) subtractor_1 (.a(A), .b(B), .out(\减 ));  // open: bin, bout
  assign \与  = A & B;  // AND_Gate and_1, 4 bits wide
  assign \或  = A | B;  // OR_Gate or_1, 4 bits wide
  Multiplexer #(.select(2), .width(4)) multiplexer_1 (
    .in0(\加 ), .in1(\减 ), .in2(\与 ), .in3(\或 ), .out(OUT), .sel(OP));  // open: en
endmodule
