// Logisim project CRC.circ as structural Verilog
module CRC (
  input  [7:0] A,
  input  [3:0] B,
  output [10:0] C
);

  wire [3:0] \除1_余数 , \除2_余数 , \除3_余数 , \除4_余数 , \除6_余数 , \除7_余数 ;
  wire [3:1] q;
  wire [3:3] \除5_余数 , \除8_余数 ;

  MOD2_4bits \u_除1  (.\被除数 (A[7:4]), .\除数 (B), .\余数 (\除1_余数 ));  // open: 商
  MOD2_4bits \u_除6  (.\被除数 ({q, 1'b0}), .\除数 (B), .\余数 (\除6_余数 ));  // open: 商
  MOD2_4bits \u_除2  (.\被除数 ({\除1_余数 [2:0], A[3]}), .\除数 (B), .\余数 (\除2_余数 ));  // open: 商
  MOD2_4bits \u_除7  (.\被除数 ({\除6_余数 [2:0], 1'b0}), .\除数 (B), .\余数 (\除7_余数 ));  // open: 商
  MOD2_4bits \u_除3  (.\被除数 ({\除2_余数 [2:0], A[2]}), .\除数 (B), .\余数 (\除3_余数 ));  // open: 商
  MOD2_4bits \u_除8  (.\被除数 ({\除7_余数 [2:0], 1'b0}), .\除数 (B), .\余数 ({\除8_余数 [3], C[2:0]}));  // open: 商
  MOD2_4bits \u_除4  (.\被除数 ({\除3_余数 [2:0], A[1]}), .\除数 (B), .\余数 (\除4_余数 ));  // open: 商
  MOD2_4bits \u_除5  (.\被除数 ({\除4_余数 [2:0], A[0]}), .\除数 (B), .\余数 ({\除5_余数 [3], q}));  // open: 商

  assign C[10:3] = A;

  // Other names for the same wires on the sheet: _3bits校验码[2:0] = C[2:0]; 原数据帧[7:0] = A; 被除数[10:3] = A; 除数[3:0] = B
endmodule

// 除法
module MOD2_4bits (
  input  [3:0] \被除数 ,
  input  [3:0] \除数 ,
  output [3:0] \余数 ,
  output \商 
);

  wire [3:0] \余数_t ;

  assign \余数_t  = \被除数  ^ \除数 ;  // XOR_Gate xor_1, 4 bits wide
  Multiplexer multiplexer_1 (.in0(1'b0), .in1(1'b1), .out(\商 ), .sel(\被除数 [3]));  // open: en
  Multiplexer #(.width(4)) multiplexer_2 (.in0(\被除数 ), .in1(\余数_t ), .out(\余数 ), .sel(\被除数 [3]));  // open: en

  // Other names for the same wires on the sheet: a[3:0] = \被除数 
endmodule
