// Logisim project GRF.circ as structural Verilog
module grf (
  input  reset,
  input  WE,
  input  clk,
  input  [4:0] A1,
  input  [4:0] A2,
  input  [4:0] A3,
  input  [31:0] WD,
  output [31:0] RD1,
  output [31:0] RD2
);

  register register_1 (
    .IN(A1), .A(WD), .IN2(A3), .IN1(A2), .CLK(clk), .RESET(reset), .enable(WE), .out(RD1), .out2(RD2));
endmodule

module register (
  input  enable,
  input  RESET,
  input  CLK,
  input  [4:0] IN,
  input  [31:0] A,
  input  [4:0] IN2,
  input  [4:0] IN1,
  output [31:0] out,
  output [31:0] out2
);

  wire [31:0] _1, _2, _3, _4, _5, _6, _7, _8, _9, _10, _11, _12, _13, _14, _15, _16, _17, _18, _19, _20, _21,
       _22, _23, _24, _25, _26, _27, _28, _29, _30, _31, _32, D2, D3, D4, D5, D6, D7, D8, D9, D10, D11, D12,
       D13, D14, D15, D16, D17, D18, D19, D20, D21, D22, D23, D24, D25, D26, D27, D28, D29, D30, D31, D32;

  Register #(.width(32)) R1 (.D({32{1'b0}}), .Q(_1), .clk(CLK), .clr(RESET));  // open: en
  Register #(.width(32)) R9 (.D(D9), .Q(_9), .clk(CLK), .clr(RESET));  // open: en
  Register #(.width(32)) R17 (.D(D17), .Q(_17), .clk(CLK), .clr(RESET));  // open: en
  Register #(.width(32)) R25 (.D(D25), .Q(_25), .clk(CLK), .clr(RESET));  // open: en
  Demultiplexer #(.select(5), .width(32), .tristate("true")) demultiplexer_1 (
    .out1(D2), .out2(D3), .out3(D4), .out4(D5), .out5(D6), .out6(D7), .out7(D8), .out8(D9), .out9(D10),
    .out10(D11), .out11(D12), .out12(D13), .out13(D14), .out14(D15), .out15(D16), .out16(D17), .out17(D18),
    .out18(D19), .out19(D20), .out20(D21), .out21(D22), .out22(D23), .out23(D24), .out24(D25), .out25(D26),
    .out26(D27), .out27(D28), .out28(D29), .out29(D30), .out30(D31), .out31(D32), .in(A), .sel(IN2),
    .en(enable));  // open: out0
  Register #(.width(32)) R2 (.D(D2), .Q(_2), .clk(CLK), .clr(RESET));  // open: en
  Register #(.width(32)) R10 (.D(D10), .Q(_10), .clk(CLK), .clr(RESET));  // open: en
  Register #(.width(32)) R18 (.D(D18), .Q(_18), .clk(CLK), .clr(RESET));  // open: en
  Register #(.width(32)) R26 (.D(D26), .Q(_26), .clk(CLK), .clr(RESET));  // open: en
  Register #(.width(32)) R3 (.D(D3), .Q(_3), .clk(CLK), .clr(RESET));  // open: en
  Register #(.width(32)) R11 (.D(D11), .Q(_11), .clk(CLK), .clr(RESET));  // open: en
  Register #(.width(32)) R19 (.D(D19), .Q(_19), .clk(CLK), .clr(RESET));  // open: en
  Register #(.width(32)) R27 (.D(D27), .Q(_27), .clk(CLK), .clr(RESET));  // open: en
  Register #(.width(32)) R4 (.D(D4), .Q(_4), .clk(CLK), .clr(RESET));  // open: en
  Register #(.width(32)) R12 (.D(D12), .Q(_12), .clk(CLK), .clr(RESET));  // open: en
  Register #(.width(32)) R20 (.D(D20), .Q(_20), .clk(CLK), .clr(RESET));  // open: en
  Register #(.width(32)) R28 (.D(D28), .Q(_28), .clk(CLK), .clr(RESET));  // open: en
  Register #(.width(32)) R5 (.D(D5), .Q(_5), .clk(CLK), .clr(RESET));  // open: en
  Register #(.width(32)) R13 (.D(D13), .Q(_13), .clk(CLK), .clr(RESET));  // open: en
  Register #(.width(32)) R21 (.D(D21), .Q(_21), .clk(CLK), .clr(RESET));  // open: en
  Register #(.width(32)) R29 (.D(D29), .Q(_29), .clk(CLK), .clr(RESET));  // open: en
  Register #(.width(32)) R6 (.D(D6), .Q(_6), .clk(CLK), .clr(RESET));  // open: en
  Register #(.width(32)) R14 (.D(D14), .Q(_14), .clk(CLK), .clr(RESET));  // open: en
  Register #(.width(32)) R22 (.D(D22), .Q(_22), .clk(CLK), .clr(RESET));  // open: en
  Register #(.width(32)) R30 (.D(D30), .Q(_30), .clk(CLK), .clr(RESET));  // open: en
  Register #(.width(32)) R7 (.D(D7), .Q(_7), .clk(CLK), .clr(RESET));  // open: en
  Register #(.width(32)) R15 (.D(D15), .Q(_15), .clk(CLK), .clr(RESET));  // open: en
  Register #(.width(32)) R23 (.D(D23), .Q(_23), .clk(CLK), .clr(RESET));  // open: en
  Register #(.width(32)) R31 (.D(D31), .Q(_31), .clk(CLK), .clr(RESET));  // open: en
  Register #(.width(32)) R8 (.D(D8), .Q(_8), .clk(CLK), .clr(RESET));  // open: en
  Register #(.width(32)) R16 (.D(D16), .Q(_16), .clk(CLK), .clr(RESET));  // open: en
  Register #(.width(32)) R24 (.D(D24), .Q(_24), .clk(CLK), .clr(RESET));  // open: en
  Register #(.width(32)) R32 (.D(D32), .Q(_32), .clk(CLK), .clr(RESET));  // open: en
  Multiplexer #(.select(5), .width(32)) multiplexer_1 (
    .in0(_1), .in1(_2), .in2(_3), .in3(_4), .in4(_5), .in5(_6), .in6(_7), .in7(_8), .in8(_9), .in9(_10),
    .in10(_11), .in11(_12), .in12(_13), .in13(_14), .in14(_15), .in15(_16), .in16(_17), .in17(_18),
    .in18(_19), .in19(_20), .in20(_21), .in21(_22), .in22(_23), .in23(_24), .in24(_25), .in25(_26),
    .in26(_27), .in27(_28), .in28(_29), .in29(_30), .in30(_31), .in31(_32), .out(out), .sel(IN));  // open: en
  Multiplexer #(.select(5), .width(32)) multiplexer_2 (
    .in0(_1), .in1(_2), .in2(_3), .in3(_4), .in4(_5), .in5(_6), .in6(_7), .in7(_8), .in8(_9), .in9(_10),
    .in10(_11), .in11(_12), .in12(_13), .in13(_14), .in14(_15), .in15(_16), .in16(_17), .in17(_18),
    .in18(_19), .in19(_20), .in20(_21), .in21(_22), .in22(_23), .in23(_24), .in24(_25), .in25(_26),
    .in26(_27), .in27(_28), .in28(_29), .in29(_30), .in30(_31), .in31(_32), .out(out2), .sel(IN1));  // open: en

  // Other names for the same wires on the sheet: EN = enable
endmodule
