// Logisim project biaodashi.circ as structural Verilog
module fsm (
  input  [1:0] In,
  input  CLR,
  output Z
);

  wire and_1_out, and_3_out, and_4_out, CLK_out, not_1_out, not_2_out, not_3_out, not_4_out, not_5_out, s0,
       s1, xor_1_out;
  wire [1:0] multiplexer_1_out, or_1_out;

  not not_1 (not_1_out, s0);
  not not_2 (not_2_out, In[0]);
  not not_3 (not_3_out, In[1]);
  xor xor_1 (xor_1_out, s0, s1);
  and and_1 (and_1_out, s1, not_2_out, not_1_out);
  and and_2 (or_1_out[1], xor_1_out, not_2_out);
  and and_3 (and_3_out, In[0], not_3_out);
  or or_1 (or_1_out[0], and_1_out, and_3_out);
  Multiplexer #(.width(2)) multiplexer_1 (.in0(or_1_out), .in1(2'b00), .out(multiplexer_1_out), .sel(CLR));  // open: en
  Register #(.width(2)) register_1 (.D(multiplexer_1_out), .Q({s1, s0}), .clk(CLK_out));  // open: en, clr
  Clock CLK (.out(CLK_out));
  not not_4 (not_4_out, s0);
  not not_5 (not_5_out, In[0]);
  and and_4 (and_4_out, not_5_out, not_4_out, s1);
  Multiplexer multiplexer_2 (.in0(1'b0), .in1(1'b1), .out(Z), .sel(and_4_out));  // open: en
endmodule
